# Fritzing sketch breadboard (saved by Fritzing 0.9.3b)
breadboards: 6

parts:
  Microcontroller = IC, DIP package, 40 pins [chip_label="Atmega 162"]
  RESET = Pushbutton [package="[SMD]"]
  LED = LED - 3mm [color="Red (633nm)" package="3 mm [THT]"]
  VCC1 = Battery block 9V
  C3 = Capacitor [package=cap-pth-small]
  U1 = Voltage Regulator - 5V [package="TO220 [THT]"]
  Clock = Crystal [frequency="4 MHz" package=THT]
  UART_transceiver = IC, DIP package, 20 pins [chip_label=MAX233]
  C4 = Capacitor [package=cap-pth-large]
  UART = male pin header, 5 pins [form="♂ (male)"]
  CAN_controller = IC, DIP package, 18 pins [chip_label=MCP2515]
  C2 = Capacitor [package=cap-pth-large]
  CAN_transceiver = IC, DIP package, 8 pins [chip_label=MC2551]  # not connected

nets:
  N1: Microcontroller.pin1, LED.anode
  N2: Microcontroller.pin3, Microcontroller.pin9, RESET.Pin_1, RESET.Pin_2
  N3: Microcontroller.pin10, UART_transceiver.pin3
  N4: Microcontroller.pin11, UART_transceiver.pin2
  N5: Microcontroller.pin18, Clock.pin_1
  N6: Microcontroller.pin19, Clock.pin_0
  GND: Microcontroller.pin20, RESET.Pin_3, RESET.Pin_4, LED.cathode, VCC1.-, C3.2, U1.GND, UART_transceiver.pin6, C4.2, CAN_controller.pin9, C2.2
  5V: Microcontroller.pin40, U1.output_voltage, UART_transceiver.pin7, C4.1, CAN_controller.pin18, C2.1
  N7: VCC1.+, C3.1, U1.input_voltage
  N8: UART_transceiver.pin4, UART.pin3
  N9: UART_transceiver.pin5, UART.pin4
  N10: UART_transceiver.pin10, UART_transceiver.pin16
  N11: UART_transceiver.pin11, UART_transceiver.pin15
  N12: UART_transceiver.pin12, UART_transceiver.pin17

notes:
  TTK4255 - Byggern, This is the breadboard for Industrial Embedded., 1
